// Logisim project addertopia.circ as structural Verilog: 1 circuit, main circuit Full Adder
module Full_Adder (
  input  in_1,
  input  in_2,
  input  in_3
);

  wire and_2_out, and_out, or_1_out, XOR_2_out, XOR_out;

  xor XOR (XOR_out, in_2, in_3);
  and \and  (and_out, in_2, in_3);
  and and_2 (and_2_out, in_1, XOR_out);
  buf XOR_2 (XOR_2_out, XOR_out);  // XOR_Gate
  or or_1 (or_1_out, and_out, and_2_out);
  // Probe on XOR_2_out
  // Probe on or_1_out
endmodule
